// Logisim project 4reg.circ as structural Verilog: 3 circuits, main circuit main
module main (
);

  Counter counter_1 ();  // open: load, D, count, Q, carry, clk, clr
  _4reg u_4reg_1 ();  // open: data_input, write_address, CLK, rs2_address, rs1_address, rs1, rs2, write_enable
endmodule

module _4reg (
  input  [7:0] data_input,
  input  [1:0] write_address,
  input  CLK,
  input  write_enable,
  input  [1:0] rs2_address,
  input  [1:0] rs1_address,
  output [7:0] rs1,
  output [7:0] rs2
);

  wire and_1_out, and_2_out, and_3_out, and_4_out, decoder_1_out0, decoder_1_out1, decoder_1_out2,
       decoder_1_out3;
  wire [7:0] register_1_q, register_2_q, register_3_q, register_4_q;

  Decoder #(.select(2), .enable("false")) decoder_1 (
    .out0(decoder_1_out0), .out1(decoder_1_out1), .out2(decoder_1_out2), .out3(decoder_1_out3),
    .sel(write_address));
  and and_1 (and_1_out, decoder_1_out0, write_enable);
  and and_2 (and_2_out, decoder_1_out1, write_enable);
  and and_3 (and_3_out, decoder_1_out2, write_enable);
  and and_4 (and_4_out, decoder_1_out3, write_enable);
  Register register_1 (.D(data_input), .en(and_1_out), .Q(register_1_q), .clk(CLK));  // open: clr
  Register register_2 (.D(data_input), .en(and_2_out), .Q(register_2_q), .clk(CLK));  // open: clr
  Register register_3 (.D(data_input), .en(and_3_out), .Q(register_3_q), .clk(CLK));  // open: clr
  Register register_4 (.D(data_input), .en(and_4_out), .Q(register_4_q), .clk(CLK));  // open: clr
  Multiplexer #(.select(2), .width(8)) multiplexer_1 (
    .in0(register_1_q), .in1(register_2_q), .in2(register_3_q), .in3(register_4_q), .out(rs1),
    .sel(rs1_address));  // open: en
  Multiplexer #(.select(2), .width(8)) multiplexer_2 (
    .in0(register_1_q), .in1(register_2_q), .in2(register_3_q), .in3(register_4_q), .out(rs2),
    .sel(rs2_address));  // open: en
endmodule

module \取指令  (
  input  \指令地址_1使能 ,
  input  CLK,
  input  reset,
  output [31:0] \指令 
);

  wire not_1_out;
  wire [3:0] adder_1_out, counter_1_q;

  not not_1 (not_1_out, \指令地址_1使能 );
  Counter #(.width(4), .max('hf)) counter_1 (
    .load(\指令地址_1使能 ), .D(adder_1_out), .count(not_1_out), .Q(counter_1_q), .clk(CLK), .clr(reset));  // open: carry
  Adder #(.width(4)) adder_1 (.a(counter_1_q), .b(4'b0001), .out(adder_1_out));  // open: cin, cout
  ROM #(.addrWidth(4), .dataWidth(32)) rom_1 (.addr(counter_1_q), .data(\指令 ));  // open: sel
endmodule
