// Logisim project ALU.circ as structural Verilog: 1 circuit, main circuit ALU
module ALU (
  input  [31:0] inputA,
  input  [31:0] inputB,
  input  [3:0] in_3,
  output [31:0] out_4
);

  wire comparator_1_lt;
  wire [31:0] adder_1_out, and_1_out, bit_extender_1_out, nor_1_out, or_1_out, subtractor_1_out;

  assign and_1_out = inputA & inputB;  // AND_Gate and_1, 32 bits wide
  assign or_1_out = inputA | inputB;  // OR_Gate or_1, 32 bits wide
  Adder #(.width(32)) adder_1 (.a(inputA), .b(inputB), .out(adder_1_out));  // open: cin, cout
  Subtractor #(.width(32)) subtractor_1 (.a(inputA), .b(inputB), .out(subtractor_1_out));  // open: bin, bout
  Comparator #(.width(32), .mode("unsigned")) comparator_1 (
    .a(inputA), .b(inputB), .lt(comparator_1_lt));  // open: gt, eq
  assign nor_1_out = ~(inputA | inputB);  // NOR_Gate nor_1, 32 bits wide
  assign bit_extender_1_out = {{31{1'b0}}, comparator_1_lt};  // Bit_Extender bit_extender_1
  Multiplexer #(.select(4), .width(32)) multiplexer_1 (
    .in0(and_1_out), .in1(or_1_out), .in2(adder_1_out), .in6(subtractor_1_out), .in7(bit_extender_1_out),
    .in12(nor_1_out), .out(out_4), .sel(in_3));  // open: in3, in4, in5, in8, in9, in10, in11, in13, in14, in15, en

  // Other names for the same wires on the sheet: A[31:0] = inputA; B[31:0] = inputB
endmodule
