// Logisim project ALUcontrol.circ as structural Verilog: 1 circuit, main circuit ALUcontrol
module ALUcontrol (
  input  [1:0] ALUOp,
  input  [5:0] F5_0,
  output [3:0] ALUcontrol
);

  wire and_1_out, or_1_out;

  and and_1 (and_1_out, ALUOp[1], F5_0[1]);
  or or_1 (or_1_out, F5_0[3], F5_0[0]);
  and and_2 (ALUcontrol[3], ALUOp[0], ~ALUOp[0]);  // AND_Gate
  or or_2 (ALUcontrol[2], ALUOp[0], and_1_out);
  or or_3 (ALUcontrol[1], ~ALUOp[1], ~F5_0[2]);  // OR_Gate
  and and_3 (ALUcontrol[0], ALUOp[1], or_1_out);
endmodule
