// Logisim project main.circ as structural Verilog: 1 circuit, main circuit main
module main (
  output [31:0] out_1,
  output [31:0] out_2,
  output [31:0] out_3
);

  wire ALUSrc, CLK, MemRead, MemWrite, not_1_out, \opcode到控制信号_1_memtoreg , RegDst, write_enable;
  wire [1:0] multiplexer_1_out, \opcode到控制信号_1_aluop2 ;
  wire [3:0] ALUcontrol;
  wire [31:0] bit_extender_1_out, data_input, \n4寄存器堆_1_rs1 , \n4寄存器堆_1_rs2 , ram_1_data;

  Clock clock_1 (.out(CLK));
  not not_1 (not_1_out, RegDst);
  \取指令  \u_取指令_1  (.\指令_1使能 (1'b1), .CLK(CLK), .\指令 (out_1));  // open: reset
  Multiplexer #(.width(2)) multiplexer_1 (
    .in0(out_1[12:11]), .in1(out_1[17:16]), .out(multiplexer_1_out), .sel(not_1_out));  // open: en
  assign bit_extender_1_out = {{16{out_1[15]}}, out_1[15:0]};  // Bit_Extender bit_extender_1
  \_4寄存器堆  \u_4寄存器堆_1  (
    .data_input(data_input), .write_address(multiplexer_1_out), .CLK(CLK), .write_enable(write_enable),
    .rs2_address(out_1[17:16]), .rs1_address(out_1[22:21]), .rs1(\n4寄存器堆_1_rs1 ), .rs2(\n4寄存器堆_1_rs2 ));
  ALU alu_1 (.inputA(\n4寄存器堆_1_rs1 ), .inputB(out_3), .out_4(out_2), .in_3(ALUcontrol));
  Multiplexer #(.width(32)) multiplexer_2 (
    .in0(\n4寄存器堆_1_rs2 ), .in1(bit_extender_1_out), .out(out_3), .sel(ALUSrc));  // open: en
  \opcode到控制信号  \opcode到控制信号_1  (
    .opcode(out_1[31:26]), .RegDst(RegDst), .ALUSrc(ALUSrc), .MemtoReg(\opcode到控制信号_1_memtoreg ),
    .RegWrite(write_enable), .MemRead(MemRead), .MemWrite(MemWrite), .ALUOp1(\opcode到控制信号_1_aluop2 [1]),
    .ALUOp2(\opcode到控制信号_1_aluop2 [0]));  // open: Branch
  ALUcontrol alucontrol_1 (.ALUcontrol(ALUcontrol), .ALUOp(\opcode到控制信号_1_aluop2 ), .F5_0(out_1[5:0]));
  RAM #(.dataWidth(32), .bus("separate")) ram_1 (
    .addr(out_2[7:0]), .din(\n4寄存器堆_1_rs2 ), .data(ram_1_data), .str(MemWrite), .clk(CLK), .ld(MemRead));  // open: sel, clr
  Multiplexer #(.width(32)) multiplexer_3 (
    .in0(out_2), .in1(ram_1_data), .out(data_input), .sel(\opcode到控制信号_1_memtoreg ));  // open: en

  // Other names for the same wires on the sheet: Funct5_0[5:0] = out_1[5:0]
endmodule
