// Logisim project 取指令.circ as structural Verilog: 1 circuit, main circuit 取指令
module \取指令  (
  input  \指令_1使能 ,
  input  CLK,
  input  reset,
  output [31:0] \指令 
);

  wire not_1_out;
  wire [3:0] counter_1_q, \下一指令 ;

  not not_1 (not_1_out, \指令_1使能 );
  Counter #(.width(4), .max('hf)) counter_1 (
    .load(\指令_1使能 ), .D(\下一指令 ), .count(not_1_out), .Q(counter_1_q), .clk(CLK), .clr(reset));  // open: carry
  Adder #(.width(4)) adder_1 (.a(4'b0001), .b(counter_1_q), .out(\下一指令 ));  // open: cin, cout
  ROM #(.addrWidth(4), .dataWidth(32)) rom_1 (.addr(counter_1_q), .data(\指令 ));  // open: sel
endmodule
