// Logisim project opcode到控制信号.circ as structural Verilog: 1 circuit, main circuit opcode到控制信号
module \opcode到控制信号  (
  input  [5:0] opcode,
  output RegDst,
  output ALUSrc,
  output MemtoReg,
  output RegWrite,
  output MemRead,
  output MemWrite,
  output Branch,
  output ALUOp1,
  output ALUOp2
);

  wire not_1_out, not_2_out, not_3_out, not_4_out, not_5_out, not_6_out;

  not not_1 (not_1_out, opcode[1]);
  or or_1 (RegDst, not_1_out, opcode[3]);
  not not_2 (not_2_out, opcode[3]);
  and and_1 (RegWrite, not_2_out, not_3_out);
  not not_3 (not_3_out, opcode[2]);
  not not_4 (not_4_out, opcode[3]);
  and and_2 (MemRead, not_4_out, opcode[1]);
  not not_5 (not_5_out, opcode[2]);
  and and_3 (ALUOp1, not_5_out, not_6_out);
  not not_6 (not_6_out, opcode[1]);

  assign ALUOp2 = opcode[2];
  assign ALUSrc = opcode[1];
  assign Branch = opcode[2];
  assign MemtoReg = opcode[1];
  assign MemWrite = opcode[3];
endmodule
